// Logisim project Final_Project.circ as structural Verilog: 4 circuits, main circuit main
module main (
  input  reset,
  input  reset_screen
);

  wire CLK, DWE, SUB, WE;
  wire [1:0] AFS, RSS;
  wire [2:0] Addr_A, Addr_B, Addr_D;
  wire [3:0] ALU_out, multiplexer_1_out, Opcode, Port_A, Port_B;
  wire [3:3] rom_1_data_2;
  wire [7:0] counter_1_q;
  wire [11:7] rom_1_data;

  Counter counter_1 (.clr(reset), .load(1'b0), .up(1'b1), .count(1'b1), .clk(CLK), .Q(counter_1_q));  // open: D, carry
  // Probe on counter_1_q
  ROM #(.dataWidth(16)) rom_1 (
    .addr(counter_1_q),
    .data({Opcode, rom_1_data[11], Addr_D, rom_1_data[7], Addr_A, rom_1_data_2[3], Addr_B}));
  // Probe on {Opcode, rom_1_data[11], Addr_D, rom_1_data[7], Addr_A, rom_1_data_2[3], Addr_B}
  // Probe on Opcode
  // Probe on Addr_D
  ROM #(.addrWidth(4), .dataWidth(7)) rom_2 (.addr(Opcode), .data({SUB, AFS, RSS, DWE, WE}));
  // Probe on Addr_A
  // Probe on {rom_1_data_2[3], Addr_B}
  // Probe on Addr_B
  Clock u_CLK (.out(CLK));
  // Probe on WE
  // Probe on DWE
  // Probe on RSS
  // Probe on AFS
  // Probe on SUB
  // Probe on multiplexer_1_out
  Multiplexer #(.select(2), .width(4), .enable("false")) multiplexer_1 (
    .in0({rom_1_data_2[3], Addr_B}), .in1(ALU_out), .in2(Port_A), .out(multiplexer_1_out), .sel(RSS));  // open: in3
  TTY tty_1 (.data({Port_A[2:0], Port_B}), .clk(CLK), .we(DWE), .clr(reset_screen));
  // Probe on Port_A
  ThreePortRegister threeportregister_1 (
    .WE(WE), .WAddr(Addr_D), .RAddrA(Addr_A), .RAddrB(Addr_B), .Port_D(multiplexer_1_out), .WCLK(CLK),
    .Port_A(Port_A), .Port_B(Port_B));
  // Probe on Port_B
  // Probe on ALU_out
  ALU alu_1 (.A(Port_A), .B(Port_B), .SUB(SUB), .AFS(AFS), .ALU_out(ALU_out));

  // Notes on the sheet:
  //   contents of rom_1 (hex, n*v repeats v):
  //   1003 2700 1102 1204 1306 170d 3027 1701 3037 1407 1500 3041 3030 1705 3037 170c 3037 3015 1605 3065
  //   3041 1701 3037 3042 1709 3037 170b 3037 3042 170f 3037 3015 3010 3002 3001 170a 3057 3002 170b 3017
  //   3001 170d 3007 7721 3007 170a 3057 3002 3017 3001 170d 3007 7722 3007 170a 3057 1708 3067 170f 3027
  //   3061 3015 3002 170d 3017 3001 3007 170f 4717 1601 7776 7727 3007 170a 3057 1605 3060 3066 3021 3015
  //   3002 170d 3017 3001 3007 f721 3007
  //   contents of rom_2 (hex, n*v repeats v):
  //   0 1 9 a 5 15 25 35 7*0 75
  //   Addr_A = Read Address for Port A
  //   Addr_B = Read Address for Port B
  //   Addr_D = Read Address for Port D
  //   Opcode = Operation Code
  //   WE = Register Write Enable
  //   DWE = Display Write Enable
  //   RSS = Register Source Select
  //   AFS = ALU Function Select
  //   SUB = Subtract
  //   Marcel Pratikto
  //   Data bits
endmodule

module ThreePortRegister (
  input  WE,
  input  [2:0] WAddr,
  input  [2:0] RAddrA,
  input  [2:0] RAddrB,
  input  [3:0] Port_D,
  input  WCLK,
  output [3:0] Port_A,
  output [3:0] Port_B
);

  wire decoder_1_out0, decoder_1_out1, decoder_1_out2, decoder_1_out3, decoder_1_out4, decoder_1_out5,
       decoder_1_out6, decoder_1_out7;
  wire [3:0] R0, R1, R2, R3, R4, R5, R6, R7;

  Decoder #(.select(3)) decoder_1 (
    .out0(decoder_1_out0), .out1(decoder_1_out1), .out2(decoder_1_out2), .out3(decoder_1_out3),
    .out4(decoder_1_out4), .out5(decoder_1_out5), .out6(decoder_1_out6), .out7(decoder_1_out7), .sel(WAddr),
    .en(WE));
  FourBitRegister fourbitregister_1 (.Din(Port_D), .Write_EN(decoder_1_out0), .CLK(WCLK), .Dout(R0));
  FourBitRegister fourbitregister_2 (.Din(Port_D), .Write_EN(decoder_1_out1), .CLK(WCLK), .Dout(R1));
  FourBitRegister fourbitregister_3 (.Din(Port_D), .Write_EN(decoder_1_out2), .CLK(WCLK), .Dout(R2));
  FourBitRegister fourbitregister_4 (.Din(Port_D), .Write_EN(decoder_1_out3), .CLK(WCLK), .Dout(R3));
  FourBitRegister fourbitregister_5 (.Din(Port_D), .Write_EN(decoder_1_out4), .CLK(WCLK), .Dout(R4));
  FourBitRegister fourbitregister_6 (.Din(Port_D), .Write_EN(decoder_1_out5), .CLK(WCLK), .Dout(R5));
  FourBitRegister fourbitregister_7 (.Din(Port_D), .Write_EN(decoder_1_out6), .CLK(WCLK), .Dout(R6));
  FourBitRegister fourbitregister_8 (.Din(Port_D), .Write_EN(decoder_1_out7), .CLK(WCLK), .Dout(R7));
  Multiplexer #(.select(3), .width(4), .enable("false")) multiplexer_1 (
    .in0(R0), .in1(R1), .in2(R2), .in3(R3), .in4(R4), .in5(R5), .in6(R6), .in7(R7), .out(Port_A), .sel(RAddrA));
  Multiplexer #(.select(3), .width(4), .enable("false")) multiplexer_2 (
    .in0(R0), .in1(R1), .in2(R2), .in3(R3), .in4(R4), .in5(R5), .in6(R6), .in7(R7), .out(Port_B), .sel(RAddrB));
endmodule

module FourBitRegister (
  input  [3:0] Din,
  input  Write_EN,
  input  CLK,
  output [3:0] Dout
);

  wire multiplexer_1_out, multiplexer_2_out, multiplexer_3_out, multiplexer_4_out;

  Multiplexer #(.enable("false")) multiplexer_1 (.in0(Dout[0]), .in1(Din[0]), .out(multiplexer_1_out), .sel(Write_EN));
  Multiplexer #(.enable("false")) multiplexer_2 (.in0(Dout[1]), .in1(Din[1]), .out(multiplexer_2_out), .sel(Write_EN));
  Multiplexer #(.enable("false")) multiplexer_3 (.in0(Dout[2]), .in1(Din[2]), .out(multiplexer_3_out), .sel(Write_EN));
  Multiplexer #(.enable("false")) multiplexer_4 (.in0(Dout[3]), .in1(Din[3]), .out(multiplexer_4_out), .sel(Write_EN));
  D_Flip_Flop d_ff_1 (.D(multiplexer_1_out), .clk(CLK), .Q(Dout[0]));  // open: Qn, preset, reset
  D_Flip_Flop d_ff_2 (.D(multiplexer_2_out), .clk(CLK), .Q(Dout[1]));  // open: Qn, preset, reset
  D_Flip_Flop d_ff_3 (.D(multiplexer_3_out), .clk(CLK), .Q(Dout[2]));  // open: Qn, preset, reset
  D_Flip_Flop d_ff_4 (.D(multiplexer_4_out), .clk(CLK), .Q(Dout[3]));  // open: Qn, preset, reset
endmodule

module ALU (
  input  [3:0] A,
  input  [3:0] B,
  input  SUB,
  input  [1:0] AFS,
  output [3:0] ALU_out
);

  wire [3:0] adder_1_out, and_1_out, multiplexer_1_out, not_1_out, or_1_out, xor_1_out;

  assign not_1_out = ~B;  // NOT_Gate not_1, 4 bits wide
  assign and_1_out = A & B;  // AND_Gate and_1, 4 bits wide
  assign or_1_out = A | B;  // OR_Gate or_1, 4 bits wide
  assign xor_1_out = A ^ B;  // XOR_Gate xor_1, 4 bits wide
  Multiplexer #(.width(4), .enable("false")) multiplexer_1 (
    .in0(B), .in1(not_1_out), .out(multiplexer_1_out), .sel(SUB));
  Adder #(.width(4)) adder_1 (.a(A), .b(multiplexer_1_out), .out(adder_1_out), .cin(SUB));  // open: cout
  // Probe on adder_1_out
  Multiplexer #(.select(2), .width(4), .enable("false")) multiplexer_2 (
    .in0(xor_1_out), .in1(and_1_out), .in2(or_1_out), .in3(adder_1_out), .out(ALU_out), .sel(AFS));
endmodule
