// Logisim project Lab3Part3.circ as structural Verilog: 1 circuit, main circuit main
module main (
  input  Cord,
  input  Voltage,
  input  Temp,
  output Alarm,
  output Fan
);

  wire not_1_out, not_2_out, or_1_out;

  not not_1 (not_1_out, Voltage);
  not not_2 (not_2_out, Cord);
  and and_1 (Alarm, not_2_out, Voltage);
  or or_1 (or_1_out, not_1_out, Cord);
  and and_2 (Fan, or_1_out, Temp);

  // Notes on the sheet:
  //   Marcel Pratikto
endmodule
