// Logisim project Lab4_build1.circ as structural Verilog: 1 circuit, main circuit main
module main (
  input  A,
  input  B,
  input  C,
  input  D,
  output X
);

  wire and_1_out, not_1_out, not_2_out, not_3_out;

  not not_1 (not_1_out, B);
  not not_2 (not_2_out, D);
  and and_1 (and_1_out, not_1_out, not_2_out);
  not not_3 (not_3_out, C);
  or or_1 (X, and_1_out, not_3_out);

  // Notes on the sheet:
  //   X = c+bd
  //   Marcel Pratikto
endmodule
