// Logisim project Lab4_build2.circ as structural Verilog: 1 circuit, main circuit main
module main (
  input  A,
  input  B,
  input  C,
  input  D,
  output X
);

  wire nand_1_out, nand_2_out, nand_3_out;

  nand nand_1 (nand_1_out, B, B);
  nand nand_2 (nand_2_out, D, D);
  nand nand_3 (nand_3_out, nand_1_out, nand_2_out);
  nand nand_4 (X, nand_3_out, C);

  // Notes on the sheet:
  //   X=c+bd using NAND gates only
  //   Marcel Pratikto
endmodule
