// Logisim project ROM.circ as structural Verilog: 1 circuit, main circuit main
module main (
  input  Clock,
  input  Right,
  input  Left,
  input  Stop,
  output R_Back,
  output R_Front,
  output L_Back,
  output L_Front
);

  ROM #(.addrWidth(4), .dataWidth(4)) rom_1 (
    .addr({Stop, Left, Right, Clock}), .data({L_Front, L_Back, R_Front, R_Back}));

  // Notes on the sheet:
  //   contents of rom_1 (hex, n*v repeats v):
  //   0 0 0 3 0 c 0 f 5 5 4 7 1 d 5 f
  //   Marcel Pratikto
  //   00030c0f55471d5
endmodule
