// Logisim project Lab8_Logisim.circ as structural Verilog
module NOR_SRLatch (
  input  R_NOR,
  input  S_NOR,
  output Q_NOR,
  output Qn_NOR
);

  nor nor_1 (Q_NOR, R_NOR, Qn_NOR);
  nor nor_2 (Qn_NOR, Q_NOR, S_NOR);
endmodule

module NAND_SRLatch (
  input  Sn_NAND,
  input  Rn_NAND,
  output Q_NAND,
  output Qn_NAND
);

  nand nand_1 (Q_NAND, Sn_NAND, Qn_NAND);
  nand nand_2 (Qn_NAND, Q_NAND, Rn_NAND);
endmodule

module Gated_DLatch (
  input  D,
  input  Gate,
  output Q_GateD,
  output Qn_GateD
);

  wire and_1_out, and_2_out, not_1_out;

  not not_1 (not_1_out, D);
  and and_1 (and_1_out, not_1_out, Gate);
  and and_2 (and_2_out, D, Gate);
  NOR_SRLatch nor_srlatch_1 (.R_NOR(and_1_out), .S_NOR(and_2_out), .Q_NOR(Q_GateD), .Qn_NOR(Qn_GateD));
endmodule

module Combined_Latches (
  input  R_NOR,
  input  S_NOR,
  input  Sn_NAND,
  input  Rn_NAND,
  input  D,
  input  Gate,
  output Q_NOR,
  output Qn_NOR,
  output Q_NAND,
  output Qn_NAND,
  output Q_GateD,
  output Qn_GateD
);

  NOR_SRLatch nor_srlatch_1 (.R_NOR(R_NOR), .S_NOR(S_NOR), .Q_NOR(Q_NOR), .Qn_NOR(Qn_NOR));
  NAND_SRLatch nand_srlatch_1 (.Sn_NAND(Sn_NAND), .Rn_NAND(Rn_NAND), .Q_NAND(Q_NAND), .Qn_NAND(Qn_NAND));
  Gated_DLatch gated_dlatch_1 (.D(D), .Gate(Gate), .Q_GateD(Q_GateD), .Qn_GateD(Qn_GateD));

  // Notes on the sheet:
  //   Marcel Pratikto
endmodule

module D_FlipFlop (
  output out_1
);

  wire clk_out, d_ff_1_qn;

  D_Flip_Flop d_ff_1 (.D(d_ff_1_qn), .clk(clk_out), .Q(out_1), .Qn(d_ff_1_qn));  // open: preset, reset
  Clock clk (.out(clk_out));
  Clock sysclk ();  // open: out

  // Notes on the sheet:
  //   Marcel Pratikto
endmodule
