// Logisim project Up_Counter.circ as structural Verilog: 2 circuits, main circuit main
module main (
  output Q2,
  output Q1,
  output Q0
);

  wire clk_out, d_ff_1_q, d_ff_2_q, d_ff_3_q, ifl_1_n0, ifl_1_n1, ifl_1_n2;

  Clock clk (.out(clk_out));
  Clock sysclk ();  // open: out
  IFL ifl_1 (.Q2(d_ff_1_q), .Q1(d_ff_2_q), .Q0(d_ff_3_q), .N2(ifl_1_n2), .N1(ifl_1_n1), .N0(ifl_1_n0));
  D_Flip_Flop d_ff_1 (.D(ifl_1_n2), .clk(clk_out), .Q(d_ff_1_q), .Qn(Q2));  // open: preset, reset
  D_Flip_Flop d_ff_2 (.D(ifl_1_n1), .clk(clk_out), .Q(d_ff_2_q), .Qn(Q1));  // open: preset, reset
  D_Flip_Flop d_ff_3 (.D(ifl_1_n0), .clk(clk_out), .Q(d_ff_3_q), .Qn(Q0));  // open: preset, reset

  // Notes on the sheet:
  //   Marcel Pratikto
endmodule

module IFL (
  input  Q2,
  input  Q1,
  input  Q0,
  output N2,
  output N1,
  output N0
);

  wire and_1_out, and_2_out, and_3_out, and_4_out, and_5_out, not_1_out, not_2_out, not_3_out, not_4_out,
       not_5_out;

  not not_1 (not_1_out, Q2);
  not not_2 (not_2_out, Q1);
  not not_3 (not_3_out, Q0);
  and and_1 (and_1_out, not_1_out, Q1, Q0);
  and and_2 (and_2_out, Q2, not_2_out);
  and and_3 (and_3_out, Q2, not_3_out);
  not not_4 (not_4_out, Q1);
  and and_4 (and_4_out, not_4_out, Q0);
  and and_5 (and_5_out, Q1, not_5_out);
  not not_5 (not_5_out, Q0);
  or or_1 (N2, and_1_out, and_2_out, and_3_out);
  or or_2 (N1, and_4_out, and_5_out);
  not not_6 (N0, Q0);

  // Notes on the sheet:
  //   This input forming logic only contains AND, OR, and NOT gates
  //   Marcel Pratikto
endmodule
